// Logisim project project.circ as structural Verilog: 13 circuits, main circuit main
module main (
);

  wire button_1_out, button_2_out, or_1_out;
  wire [31:0] counter_1_q, player_move_1__0, player_move_1__1, pull_resistor_1_node;

  Button button_1 (.out(button_1_out));
  Button button_2 (.out(button_2_out));
  Player_Move player_move_1 (.in_1(button_2_out), .in_2(button_1_out), ._0(player_move_1__0), ._1(player_move_1__1));
  or or_1 (or_1_out, button_1_out, button_2_out);
  // Probe on counter_1_q
  Counter #(.width(32), .max('h1f)) counter_1 (
    .load(button_1_out), .Q(counter_1_q), .clk(or_1_out));  // open: D, count, carry, clr
  Pull_Resistor pull_resistor_1 (.node(pull_resistor_1_node));
  DotMatrix #(.inputtype("row"), .matrixcols(32), .matrixrows(32)) dotmatrix_1 (
    .row0(pull_resistor_1_node), .row1(pull_resistor_1_node), .row2(pull_resistor_1_node),
    .row3(pull_resistor_1_node), .row4(pull_resistor_1_node), .row5(pull_resistor_1_node),
    .row6(pull_resistor_1_node), .row7(pull_resistor_1_node), .row8(pull_resistor_1_node),
    .row9(pull_resistor_1_node), .row10(pull_resistor_1_node), .row11(pull_resistor_1_node),
    .row12(pull_resistor_1_node), .row13(pull_resistor_1_node), .row14(pull_resistor_1_node),
    .row15(pull_resistor_1_node), .row16(pull_resistor_1_node), .row17(pull_resistor_1_node),
    .row18(pull_resistor_1_node), .row19(pull_resistor_1_node), .row20(pull_resistor_1_node),
    .row21(pull_resistor_1_node), .row22(pull_resistor_1_node), .row23(pull_resistor_1_node),
    .row24(pull_resistor_1_node), .row25(pull_resistor_1_node), .row26(pull_resistor_1_node),
    .row27(pull_resistor_1_node), .row28(pull_resistor_1_node), .row29(pull_resistor_1_node),
    .row30(player_move_1__1), .row31(player_move_1__0));
endmodule

module \трансформатор  (
  input  [4:0] in_1,
  output [31:0] out_2
);

  Comparator #(.width(5), .mode("unsigned")) comparator_1 (.a(in_1), .b({5{1'b0}}), .eq(out_2[0]));  // open: gt, lt
  Comparator #(.width(5), .mode("unsigned")) comparator_2 (.a(in_1), .b(5'b00001), .eq(out_2[1]));  // open: gt, lt
  Comparator #(.width(5), .mode("unsigned")) comparator_3 (.a(in_1), .b(5'b00010), .eq(out_2[2]));  // open: gt, lt
  Comparator #(.width(5), .mode("unsigned")) comparator_4 (.a(in_1), .b(5'b00011), .eq(out_2[3]));  // open: gt, lt
  Comparator #(.width(5), .mode("unsigned")) comparator_5 (.a(in_1), .b(5'b00100), .eq(out_2[4]));  // open: gt, lt
  Comparator #(.width(5), .mode("unsigned")) comparator_6 (.a(in_1), .b(5'b00101), .eq(out_2[5]));  // open: gt, lt
  Comparator #(.width(5), .mode("unsigned")) comparator_7 (.a(in_1), .b(5'b00110), .eq(out_2[6]));  // open: gt, lt
  Comparator #(.width(5), .mode("unsigned")) comparator_8 (.a(in_1), .b(5'b00111), .eq(out_2[7]));  // open: gt, lt
  Comparator #(.width(5), .mode("unsigned")) comparator_9 (.a(in_1), .b(5'b01000), .eq(out_2[8]));  // open: gt, lt
  Comparator #(.width(5), .mode("unsigned")) comparator_10 (.a(in_1), .b(5'b01001), .eq(out_2[9]));  // open: gt, lt
  Comparator #(.width(5), .mode("unsigned")) comparator_11 (.a(in_1), .b(5'b01010), .eq(out_2[10]));  // open: gt, lt
  Comparator #(.width(5), .mode("unsigned")) comparator_12 (.a(in_1), .b(5'b01011), .eq(out_2[11]));  // open: gt, lt
  Comparator #(.width(5), .mode("unsigned")) comparator_13 (.a(in_1), .b(5'b01100), .eq(out_2[12]));  // open: gt, lt
  Comparator #(.width(5), .mode("unsigned")) comparator_14 (.a(in_1), .b(5'b01101), .eq(out_2[13]));  // open: gt, lt
  Comparator #(.width(5), .mode("unsigned")) comparator_15 (.a(in_1), .b(5'b01110), .eq(out_2[14]));  // open: gt, lt
  Comparator #(.width(5), .mode("unsigned")) comparator_16 (.a(in_1), .b(5'b01111), .eq(out_2[15]));  // open: gt, lt
  Comparator #(.width(5), .mode("unsigned")) comparator_17 (.a(in_1), .b(5'b10000), .eq(out_2[16]));  // open: gt, lt
  Comparator #(.width(5), .mode("unsigned")) comparator_18 (.a(in_1), .b(5'b10001), .eq(out_2[17]));  // open: gt, lt
  Comparator #(.width(5), .mode("unsigned")) comparator_19 (.a(in_1), .b(5'b10010), .eq(out_2[18]));  // open: gt, lt
  Comparator #(.width(5), .mode("unsigned")) comparator_20 (.a(in_1), .b(5'b10011), .eq(out_2[19]));  // open: gt, lt
  Comparator #(.width(5), .mode("unsigned")) comparator_21 (.a(in_1), .b(5'b10100), .eq(out_2[20]));  // open: gt, lt
  Comparator #(.width(5), .mode("unsigned")) comparator_22 (.a(in_1), .b(5'b10101), .eq(out_2[21]));  // open: gt, lt
  Comparator #(.width(5), .mode("unsigned")) comparator_23 (.a(in_1), .b(5'b10110), .eq(out_2[22]));  // open: gt, lt
  Comparator #(.width(5), .mode("unsigned")) comparator_24 (.a(in_1), .b(5'b10111), .eq(out_2[23]));  // open: gt, lt
  Comparator #(.width(5), .mode("unsigned")) comparator_25 (.a(in_1), .b(5'b11000), .eq(out_2[24]));  // open: gt, lt
  Comparator #(.width(5), .mode("unsigned")) comparator_26 (.a(in_1), .b(5'b11001), .eq(out_2[25]));  // open: gt, lt
  Comparator #(.width(5), .mode("unsigned")) comparator_27 (.a(in_1), .b(5'b11010), .eq(out_2[26]));  // open: gt, lt
  Comparator #(.width(5), .mode("unsigned")) comparator_28 (.a(in_1), .b(5'b11011), .eq(out_2[27]));  // open: gt, lt
  Comparator #(.width(5), .mode("unsigned")) comparator_29 (.a(in_1), .b(5'b11100), .eq(out_2[28]));  // open: gt, lt
  Comparator #(.width(5), .mode("unsigned")) comparator_30 (.a(in_1), .b(5'b11101), .eq(out_2[29]));  // open: gt, lt
  Comparator #(.width(5), .mode("unsigned")) comparator_31 (.a(in_1), .b(5'b11110), .eq(out_2[30]));  // open: gt, lt
  Comparator #(.width(5), .mode("unsigned")) comparator_32 (.a(in_1), .b({5{1'b1}}), .eq(out_2[31]));  // open: gt, lt
endmodule

module \инкремент  (
  input  [4:0] X,
  output [4:0] R,
  output Cout
);

  wire [4:1] and_1_out;

  assign {Cout, and_1_out} = {and_1_out, 1'b1} & X;  // AND_Gate and_1, 5 bits wide
  assign R = X ^ {and_1_out, 1'b1};  // XOR_Gate xor_1, 5 bits wide
endmodule

module \декремент  (
  input  [7:0] X,
  output [7:0] R,
  output Cout
);

  wire [7:1] and_1_out;
  wire [7:7] and_1_out_2;

  assign R = ~(X ^ ~{and_1_out, 1'b1});  // XNOR_Gate xnor_1, 8 bits wide
  assign {and_1_out_2[7], and_1_out} = ~X & {and_1_out, 1'b1};  // AND_Gate and_1, 8 bits wide
  Multiplexer #(.disabled(0), .enable("false")) multiplexer_1 (
    .in0(1'b1), .in1(1'b0), .out(Cout), .sel(and_1_out_2[7]));
endmodule

module T_Block (
  input  A,
  input  B,
  input  C,
  output OUT
);

  or or_1 (OUT, A, B, C);
endmodule

module Player_Move (
  input  in_1,
  input  in_2,
  output [31:0] _0,
  output [31:0] _1
);

  wire or_1_out;
  wire [31:0] counter_1_q;

  T_Block t_block_1 (.A(_1[22]), .B(_1[24]), .C(_1[23]), .OUT(_0[23]));
  T_Block t_block_2 (.A(_1[21]), .B(_1[23]), .C(_1[22]), .OUT(_0[22]));
  T_Block t_block_3 (.A(_1[20]), .B(_1[22]), .C(_1[21]), .OUT(_0[21]));
  T_Block t_block_4 (.A(_1[19]), .B(_1[21]), .C(_1[20]), .OUT(_0[20]));
  T_Block t_block_5 (.A(_1[18]), .B(_1[20]), .C(_1[19]), .OUT(_0[19]));
  T_Block t_block_6 (.A(_1[17]), .B(_1[19]), .C(_1[18]), .OUT(_0[18]));
  T_Block t_block_7 (.A(_1[31]), .B(_1[1]), .C(_1[0]), .OUT(_0[0]));
  T_Block t_block_8 (.A(_1[16]), .B(_1[18]), .C(_1[17]), .OUT(_0[17]));
  T_Block t_block_9 (.A(_1[0]), .B(_1[2]), .C(_1[1]), .OUT(_0[1]));
  T_Block t_block_10 (.A(_1[1]), .B(_1[3]), .C(_1[2]), .OUT(_0[2]));
  T_Block t_block_11 (.A(_1[15]), .B(_1[17]), .C(_1[16]), .OUT(_0[16]));
  T_Block t_block_12 (.A(_1[2]), .B(_1[4]), .C(_1[3]), .OUT(_0[3]));
  T_Block t_block_13 (.A(_1[3]), .B(_1[5]), .C(_1[4]), .OUT(_0[4]));
  T_Block t_block_14 (.A(_1[14]), .B(_1[16]), .C(_1[15]), .OUT(_0[15]));
  T_Block t_block_15 (.A(_1[13]), .B(_1[15]), .C(_1[14]), .OUT(_0[14]));
  T_Block t_block_16 (.A(_1[12]), .B(_1[14]), .C(_1[13]), .OUT(_0[13]));
  T_Block t_block_17 (.A(_1[11]), .B(_1[13]), .C(_1[12]), .OUT(_0[12]));
  T_Block t_block_18 (.A(_1[10]), .B(_1[12]), .C(_1[11]), .OUT(_0[11]));
  T_Block t_block_19 (.A(_1[9]), .B(_1[11]), .C(_1[10]), .OUT(_0[10]));
  T_Block t_block_20 (.A(_1[8]), .B(_1[10]), .C(_1[9]), .OUT(_0[9]));
  T_Block t_block_21 (.A(_1[7]), .B(_1[9]), .C(_1[8]), .OUT(_0[8]));
  T_Block t_block_22 (.A(_1[4]), .B(_1[6]), .C(_1[5]), .OUT(_0[5]));
  T_Block t_block_23 (.A(_1[5]), .B(_1[6]), .C(_1[7]), .OUT(_0[6]));
  T_Block t_block_24 (.A(_1[25]), .B(_1[24]), .C(_1[23]), .OUT(_0[24]));
  T_Block t_block_25 (.A(_1[26]), .B(_1[25]), .C(_1[27]), .OUT(_0[26]));
  T_Block t_block_26 (.A(_1[27]), .B(_1[26]), .C(_1[28]), .OUT(_0[27]));
  T_Block t_block_27 (.A(_1[28]), .B(_1[27]), .C(_1[29]), .OUT(_0[28]));
  T_Block t_block_28 (.A(_1[31]), .B(_1[29]), .C(_1[30]), .OUT(_0[30]));
  T_Block t_block_29 (.A(_1[31]), .B(_1[30]), .C(_1[0]), .OUT(_0[31]));
  T_Block t_block_30 (.A(_1[25]), .B(_1[24]), .C(_1[26]), .OUT(_0[25]));
  T_Block t_block_31 (.A(_1[30]), .B(_1[29]), .C(_1[28]), .OUT(_0[29]));
  T_Block t_block_32 (.A(_1[6]), .B(_1[7]), .C(_1[8]), .OUT(_0[7]));
  // Probe on counter_1_q
  Counter #(.width(32), .max('h1f)) counter_1 (
    .load(in_1), .Q(counter_1_q), .clk(or_1_out));  // open: D, count, carry, clr
  or or_1 (or_1_out, in_1, in_2);
  \трансформатор  \u_трансформатор_1  (.in_1(counter_1_q[4:0]), .out_2(_1));
endmodule

module \богегознаетчто  (
);

  wire and_1_out, cdm_8_mark5_1_data_inst, cdm_8_mark5_1_mem_cycle, cdm_8_mark5_1_mem_read, code, data,
       not_1_out, write;
  wire [7:0] cdm_8_mark5_1_addr, cdm_8_mark5_1_data_out, cdm_8_mark5_1_r0, cdm_8_mark5_1_r1,
       cdm_8_mark5_1_r2, cdm_8_mark5_1_r3, controlled_buffer_1_out, controlled_buffer_2_out, register_1_q;

  CdM_8_mark5 cdm_8_mark5_1 (
    .addr(cdm_8_mark5_1_addr), .mem_read(cdm_8_mark5_1_mem_read), .mem_cycle(cdm_8_mark5_1_mem_cycle),
    .data_inst(cdm_8_mark5_1_data_inst), .data_out(cdm_8_mark5_1_data_out),
    .data_in(controlled_buffer_2_out), .r0(cdm_8_mark5_1_r0), .r1(cdm_8_mark5_1_r1), .r2(cdm_8_mark5_1_r2),
    .r3(cdm_8_mark5_1_r3));  // open: clock, PC, SP, PS, IAck, IRQ, vec, reset
  Decoder decoder_1 (.out0(code), .out1(data), .sel(cdm_8_mark5_1_data_inst), .en(cdm_8_mark5_1_mem_cycle));
  assign controlled_buffer_1_out = not_1_out ? cdm_8_mark5_1_data_out : 8'bz;  // Controlled_Buffer controlled_buffer_1
  not not_1 (not_1_out, cdm_8_mark5_1_mem_read);
  assign controlled_buffer_2_out = cdm_8_mark5_1_mem_read ? controlled_buffer_1_out : 8'bz;  // Controlled_Buffer controlled_buffer_2
  and and_1 (and_1_out, cdm_8_mark5_1_addr[0], cdm_8_mark5_1_addr[1], cdm_8_mark5_1_addr[2], cdm_8_mark5_1_addr[3], cdm_8_mark5_1_addr[4], cdm_8_mark5_1_addr[6], cdm_8_mark5_1_addr[7], data, write, write);
  Register register_1 (.D(cdm_8_mark5_1_data_out), .en(and_1_out), .Q(register_1_q));  // open: clk, clr
  RAM ram_1 (
    .addr(cdm_8_mark5_1_addr), .data(controlled_buffer_1_out), .sel(data), .ld(cdm_8_mark5_1_mem_read));  // open: clk, clr
  ROM #(.addrWidth(12)) rom_1 (
    .addr({register_1_q[3:0], controlled_buffer_1_out}), .data(controlled_buffer_1_out), .sel(code));
endmodule

module \монстр__т  (
  output [7:0] \_4строка ,
  output [7:0] \_3строка ,
  output [7:0] \_2строка ,
  output [7:0] \_1строка 
);


  assign \_1строка  = 8'h24;
  assign \_2строка  = 8'h5a;
  assign \_3строка  = 8'h18;
  assign \_4строка  = 8'h24;
endmodule

module \монстр__майн  (
  output [7:0] \_4строка ,
  output [7:0] \_3строка ,
  output [7:0] \_2строка ,
  output [7:0] \_1строка 
);


  assign \_1строка  = 8'h18;
  assign \_2строка  = 8'h24;
  assign \_3строка  = 8'h18;
  assign \_4строка  = 8'h24;
endmodule

module \стенка  (
  output [7:0] \_4строка ,
  output [7:0] \_3строка ,
  output [7:0] \_2строка ,
  output [7:0] \_1строка 
);


  assign \_1строка  = {8{1'b0}};
  assign \_2строка  = {8{1'b0}};
  assign \_3строка  = {8{1'b0}};
  assign \_4строка  = 8'h3c;
endmodule

module transpon (
  input  [31:0] in_1,
  input  [31:0] in_2,
  input  [31:0] in_3,
  input  [31:0] in_4,
  input  [31:0] in_5,
  input  [31:0] in_6,
  input  [31:0] in_7,
  input  [31:0] in_8,
  input  [31:0] in_9,
  input  [31:0] in_10,
  input  [31:0] in_11,
  input  [31:0] in_12,
  input  [31:0] in_13,
  input  [31:0] in_14,
  input  [31:0] in_15,
  input  [31:0] in_16,
  input  [31:0] in_17,
  input  [31:0] in_18,
  input  [31:0] in_19,
  input  [31:0] in_20,
  input  [31:0] in_21,
  input  [31:0] in_22,
  input  [31:0] in_23,
  input  [31:0] in_24,
  input  [31:0] in_25,
  input  [31:0] in_26,
  input  [31:0] in_27,
  input  [31:0] in_28,
  input  [31:0] in_29,
  input  [31:0] in_30,
  input  [31:0] in_31,
  input  [31:0] in_32,
  input  [31:0] in_33,
  output [31:0] _0,
  output [31:0] _1,
  output [31:0] _2,
  output [31:0] _3,
  output [31:0] _4,
  output [31:0] _5,
  output [31:0] out_40,
  output [31:0] _7
);


  assign _0 = {in_4[0], in_32[0], in_31[0], in_30[0], in_29[0], in_28[0], in_27[0], in_26[0], in_25[0], in_24[0], in_22[0], in_21[0], in_20[0], in_19[0], in_18[0], in_17[0], in_16[0], in_15[0], in_14[0], in_13[0], in_12[0], in_11[0], in_10[0], in_9[0], in_8[0], in_7[0], in_6[0], in_5[0], in_4[0], in_3[0], in_2[0], in_1[0]};
  assign _1 = {in_4[1], in_32[1], in_31[1], in_30[1], in_29[1], in_28[1], in_27[1], in_26[1], in_25[1], in_24[1], in_22[1], in_21[1], in_20[1], in_19[1], in_18[1], in_17[1], in_16[1], in_15[1], in_14[1], in_13[1], in_12[1], in_11[1], in_10[1], in_9[1], in_8[1], in_7[1], in_6[1], in_5[1], in_4[1], in_3[1], in_2[1], in_1[1]};
  assign _2 = {in_4[2], in_32[2], in_31[2], in_30[2], in_29[2], in_28[2], in_27[2], in_26[2], in_25[2], in_24[2], in_22[2], in_21[2], in_20[2], in_19[2], in_18[2], in_17[2], in_16[2], in_15[2], in_14[2], in_13[2], in_12[2], in_11[2], in_10[2], in_9[2], in_8[2], in_7[2], in_6[2], in_5[2], in_4[2], in_3[2], in_2[2], in_1[2]};
  assign _3 = {in_4[3], in_32[3], in_31[3], in_30[3], in_29[3], in_28[3], in_27[3], in_26[3], in_25[3], in_24[3], in_22[3], in_21[3], in_20[3], in_19[3], in_18[3], in_17[3], in_16[3], in_15[3], in_14[3], in_13[3], in_12[3], in_11[3], in_10[3], in_9[3], in_8[3], in_7[3], in_6[3], in_5[3], in_4[3], in_3[3], in_2[3], in_1[3]};
  assign _4 = {in_4[4], in_32[4], in_31[4], in_30[4], in_29[4], in_28[4], in_27[4], in_26[4], in_25[4], in_24[4], in_22[4], in_21[4], in_20[4], in_19[4], in_18[4], in_17[4], in_16[4], in_15[4], in_14[4], in_13[4], in_12[4], in_11[4], in_10[4], in_9[4], in_8[4], in_7[4], in_6[4], in_5[4], in_4[4], in_3[4], in_2[4], in_1[4]};
  assign _5 = {in_4[5], in_32[5], in_31[5], in_30[5], in_29[5], in_28[5], in_27[5], in_26[5], in_25[5], in_24[5], in_22[5], in_21[5], in_20[5], in_19[5], in_18[5], in_17[5], in_16[5], in_15[5], in_14[5], in_13[5], in_12[5], in_11[5], in_10[5], in_9[5], in_8[5], in_7[5], in_6[5], in_5[5], in_4[5], in_3[5], in_2[5], in_1[5]};
  assign _7 = {in_4[7], in_32[7], in_31[7], in_30[7], in_29[7], in_28[7], in_27[7], in_26[7], in_25[7], in_24[7], in_22[7], in_21[7], in_20[7], in_19[7], in_18[7], in_17[7], in_16[7], in_15[7], in_14[7], in_13[7], in_12[7], in_11[7], in_10[7], in_9[7], in_8[7], in_7[7], in_6[7], in_5[7], in_4[7], in_3[7], in_2[7], in_1[7]};
  assign out_40 = {in_4[6], in_32[6], in_31[6], in_30[6], in_29[6], in_28[6], in_27[6], in_26[6], in_25[6], in_24[6], in_22[6], in_21[6], in_20[6], in_19[6], in_18[6], in_17[6], in_16[6], in_15[6], in_14[6], in_13[6], in_12[6], in_11[6], in_10[6], in_9[6], in_8[6], in_7[6], in_6[6], in_5[6], in_4[6], in_3[6], in_2[6], in_1[6]};

  // Other names for the same wires on the sheet: _0_t[31:0] = in_1; _1_t[31:0] = in_2; _2_t[31:0] = in_3;
  //   _3_t[31:0] = in_4; _4_t[31:0] = in_5; _5_t[31:0] = in_6; _6[31:0] = in_7; _7_t[31:0] = in_8; _8[31:0] = in_9;
  //   _9[31:0] = in_10; _10[31:0] = in_11; _11[31:0] = in_12; _12[31:0] = in_13; _13[31:0] = in_14; _14[31:0] = in_15;
  //   _15[31:0] = in_16; _16[31:0] = in_17; _17[31:0] = in_18; _18[31:0] = in_19; _19[31:0] = in_20;
  //   _20[31:0] = in_21; _21[31:0] = in_22; _23[31:0] = in_24; _24[31:0] = in_25; _25[31:0] = in_26;
  //   _26[31:0] = in_27; _27[31:0] = in_28; _28[31:0] = in_29; _29[31:0] = in_30; _30[31:0] = in_31;
  //   _31[31:0] = in_32; _22[31:0] = in_23; _32[31:0] = in_33
endmodule

module test (
);

  wire button_1_out, button_2_out, or_1_out;
  wire [31:0] counter_1_q, dotmatrix_2_p7, dotmatrix_2_p8, dotmatrix_2_p9, dotmatrix_2_p10, dotmatrix_2_p11,
       dotmatrix_2_p12, dotmatrix_2_p13, dotmatrix_2_p14, player_move_1__0, transpon_1__0, transpon_1__1,
       transpon_1__2, transpon_1__3, transpon_1__4, transpon_1__5, transpon_1__7, transpon_1_out_40;

  DotMatrix #(.matrixcols(32), .matrixrows(32)) dotmatrix_1 (
    .col0(player_move_1__0), .col1(player_move_1__0));  // open: col2, col3, col4, col5, col6, col7, col8, col9, col10, col11, col12, col13, col14, col15, col16, col17, col18, col19, col20, col21, col22, col23, col24, col25, col26, col27, col28, col29, col30, col31
  Button button_1 (.out(button_1_out));
  Button button_2 (.out(button_2_out));
  Player_Move player_move_1 (.in_1(button_2_out), .in_2(button_1_out), ._0(player_move_1__0));  // open: _1
  Counter #(.width(32), .max('h1f)) counter_1 (
    .load(button_1_out), .Q(counter_1_q), .clk(or_1_out));  // open: D, count, carry, clr
  or or_1 (or_1_out, button_1_out, button_2_out);
  // Probe on counter_1_q
  transpon transpon_1 (
    .in_1(player_move_1__0), .in_2(player_move_1__0), ._0(transpon_1__0), ._1(transpon_1__1),
    ._2(transpon_1__2), ._3(transpon_1__3), ._4(transpon_1__4), ._5(transpon_1__5),
    .out_40(transpon_1_out_40), ._7(transpon_1__7));  // open: in_3, in_4, in_5, in_6, in_7, in_8, in_9, in_10, in_11, in_12, in_13, in_14, in_15, in_16, in_17, in_18, in_19, in_20, in_21, in_22, in_23, in_24, in_25, in_26, in_27, in_28, in_29, in_30, in_31, in_32, in_33
  // DotMatrix #(.inputtype("row"), .matrixcols(32), .matrixrows(32)) dotmatrix_2: pin names not known; wires that end beside it: transpon_1__5, transpon_1__4, transpon_1__3, transpon_1__2, transpon_1__1, transpon_1__0, dotmatrix_2_p7, dotmatrix_2_p8, dotmatrix_2_p9, dotmatrix_2_p10, dotmatrix_2_p11, dotmatrix_2_p12, dotmatrix_2_p13, dotmatrix_2_p14
  \Перевернуть  \u_перевернуть_1  (.in_1(transpon_1__7), .out_2(dotmatrix_2_p7));
  \Перевернуть  \u_перевернуть_2  (.in_1(transpon_1_out_40), .out_2(dotmatrix_2_p8));
  \Перевернуть  \u_перевернуть_3  (.in_1(transpon_1__5), .out_2(dotmatrix_2_p9));
  \Перевернуть  \u_перевернуть_4  (.in_1(transpon_1__4), .out_2(dotmatrix_2_p10));
  \Перевернуть  \u_перевернуть_5  (.in_1(transpon_1__3), .out_2(dotmatrix_2_p11));
  \Перевернуть  \u_перевернуть_6  (.in_1(transpon_1__2), .out_2(dotmatrix_2_p12));
  \Перевернуть  \u_перевернуть_7  (.in_1(transpon_1__1), .out_2(dotmatrix_2_p13));
  \Перевернуть  \u_перевернуть_8  (.in_1(transpon_1__0), .out_2(dotmatrix_2_p14));
endmodule

module \Перевернуть  (
  input  [31:0] in_1,
  output [31:0] out_2
);


  assign out_2 = {in_1[0], in_1[1], in_1[2], in_1[3], in_1[4], in_1[5], in_1[6], in_1[7], in_1[8], in_1[9], in_1[10], in_1[11], in_1[12], in_1[13], in_1[14], in_1[15], in_1[16], in_1[17], in_1[18], in_1[19], in_1[20], in_1[21], in_1[22], in_1[23], in_1[24], in_1[25], in_1[26], in_1[27], in_1[28], in_1[29], in_1[30], in_1[31]};
endmodule
